// Logisim project demultiplexer.circ as structural Verilog: 1 circuit, main circuit main
module main (
);

  wire and_1_out, and_2_out, and_3_out, and_4_out, and_5_out, and_6_out, and_7_out, and_8_out, c1_out, c2_out;

  Button c1 (.out(c1_out));
  Button c2 (.out(c2_out));
  not not_1 (c2_out, c1_out);
  Button c3 (.out(c2_out));
  not not_2 (c2_out, c2_out);
  not not_3 (c2_out, c2_out);
  and and_1 (and_1_out, c2_out, c2_out, c1_out, 1'b1);
  and and_2 (and_2_out, c2_out, 1'b1, c1_out, c2_out);
  and and_3 (and_3_out, c2_out, c2_out, c2_out, 1'b1);
  and and_4 (and_4_out, c2_out, c2_out, c1_out, 1'b1);
  and and_5 (and_5_out, c2_out, c2_out, c2_out, 1'b1);
  and and_6 (and_6_out, c1_out, c2_out, c2_out, 1'b1);
  and and_7 (and_7_out, c2_out, c2_out, c2_out, 1'b1);
  and and_8 (and_8_out, c2_out, c2_out, c2_out, 1'b1);
endmodule
