// Logisim project gen_dmux.circ as structural Verilog: 1 circuit, main circuit main
module main (
  input  in,
  input  c1,
  input  c2,
  input  c3,
  output o1,
  output o2,
  output o3,
  output o4,
  output o5,
  output o6,
  output o7,
  output o8
);

  wire not_1_out, not_2_out, not_3_out, not_4_out, not_5_out, not_6_out, not_7_out, not_8_out, not_9_out,
       not_10_out, not_11_out, not_12_out;

  not not_1 (not_1_out, c1);
  not not_2 (not_2_out, c2);
  not not_3 (not_3_out, c1);
  not not_4 (not_4_out, c3);
  not not_5 (not_5_out, c1);
  not not_6 (not_6_out, c2);
  not not_7 (not_7_out, c3);
  not not_8 (not_8_out, c2);
  not not_9 (not_9_out, c3);
  and and_1 (o7, in, c1, c2, c3);
  not not_10 (not_10_out, c1);
  not not_11 (not_11_out, c2);
  not not_12 (not_12_out, c3);
  and and_2 (o1, in, not_1_out, not_2_out, c3);
  and and_3 (o2, in, not_3_out, c2, not_4_out);
  and and_4 (o3, in, not_5_out, c2, c3);
  and and_5 (o4, in, c1, not_6_out, not_7_out);
  and and_6 (o5, in, c1, not_8_out, c3);
  and and_7 (o6, in, c1, c2, not_9_out);
  and and_8 (o8, in, not_10_out, not_11_out, not_12_out);
endmodule
