// Logisim project sign_magnitude_adder.circ as structural Verilog: 4 circuits, main circuit main
module main (
  input  in_1,
  input  in_2,
  input  in_3,
  input  in_4,
  input  in_5,
  input  in_6,
  input  in_7,
  input  in_8,
  input  in_9,
  input  in_10,
  input  in_11,
  input  in_12,
  input  in_13,
  input  in_14,
  input  in_15,
  input  in_16
);

  wire signs_eq;

  signs signs (.s1(in_8), .s2(in_9), .eq(signs_eq));
endmodule

module signs (
  input  s1,
  input  s2,
  output eq
);

  wire and_1_out, and_2_out, not_1_out, not_2_out;

  not not_1 (not_1_out, s1);
  not not_2 (not_2_out, s2);
  and and_1 (and_1_out, s1, s2);
  and and_2 (and_2_out, not_1_out, not_2_out);
  or or_1 (eq, and_1_out, and_2_out);
endmodule

module adder (
  input  cin,
  input  b1,
  input  b2,
  output sum,
  output cout
);

  wire and_1_out, and_2_out, and_3_out, and_4_out, and_5_out, and_6_out, and_7_out, and_8_out, not_1_out,
       not_2_out, not_3_out, not_4_out, not_5_out, not_6_out, not_7_out, not_8_out, not_9_out;

  not not_1 (not_1_out, b2);
  not not_2 (not_2_out, cin);
  not not_3 (not_3_out, b1);
  not not_4 (not_4_out, cin);
  not not_5 (not_5_out, b1);
  not not_6 (not_6_out, b2);
  not not_7 (not_7_out, cin);
  not not_8 (not_8_out, b2);
  not not_9 (not_9_out, b1);
  and and_1 (and_1_out, b1, b2, cin);
  and and_2 (and_2_out, b1, not_1_out, not_2_out);
  and and_3 (and_3_out, not_3_out, b2, not_4_out);
  and and_4 (and_4_out, not_5_out, not_6_out, cin);
  and and_5 (and_5_out, b1, b2, cin);
  and and_6 (and_6_out, b1, b2, not_7_out);
  and and_7 (and_7_out, b1, not_8_out, cin);
  and and_8 (and_8_out, not_9_out, b2, cin);
  or or_1 (sum, and_1_out, and_2_out, and_3_out, and_4_out);
  or or_2 (cout, and_5_out, and_6_out, and_7_out, and_8_out);
endmodule

module full_adder (
  input  a1,
  input  a2,
  input  a3,
  input  a4,
  input  a5,
  input  a6,
  input  a7,
  input  a8,
  input  b1,
  input  b2,
  input  b3,
  input  b4,
  input  b5,
  input  b6,
  input  b7,
  input  b8,
  output s1,
  output s2,
  output s3,
  output s4,
  output s5,
  output s6,
  output s7,
  output s8,
  output c
);

  wire adder_2_cout, adder_3_cout, adder_4_cout, adder_5_cout, adder_6_cout, adder_7_cout;

  adder adder_1 (.cin(a7), .b1(a8), .b2(b8), .sum(s1), .cout(a7));
  Pull_Resistor pull_resistor_1 ();  // open: node
  adder adder_2 (.cin(a7), .b1(a7), .b2(a7), .sum(s2), .cout(adder_2_cout));
  adder adder_3 (.cin(adder_2_cout), .b1(a6), .b2(b6), .sum(s3), .cout(adder_3_cout));
  adder adder_4 (.cin(adder_3_cout), .b1(a5), .b2(b5), .sum(s4), .cout(adder_4_cout));
  adder adder_5 (.cin(adder_4_cout), .b1(a4), .b2(b4), .sum(s5), .cout(adder_5_cout));
  adder adder_6 (.cin(adder_5_cout), .b1(a3), .b2(b3), .sum(s6), .cout(adder_6_cout));
  adder adder_7 (.cin(adder_6_cout), .b1(a2), .b2(b2), .sum(s7), .cout(adder_7_cout));
  adder adder_8 (.cin(adder_7_cout), .b1(a1), .b2(b1), .sum(s8), .cout(c));

  assign b7 = a7;
endmodule
